// Digital circuit 74193.dig as structural Verilog
// Synchronous 4-Bit Up/Down Binary Counter with Dual Clock
module _74193 (
  input  DN,
  input  UP,
  input  D0,
  input  D1,
  input  D2,
  input  D3,
  input  CLR,
  input  nLD,
  input  VCC,
  input  GND,
  output nBO,
  output nCO,
  output Q0,
  output Q1,
  output Q2,
  output Q3
);

  wire and_1_out, and_2_out, and_3_out, and_4_out, and_5_out, and_6_out, jk_ff_as_1_nq, jk_ff_as_2_nq,
       jk_ff_as_3_nq, jk_ff_as_4_nq, nand_1_out, nand_2_out, nand_3_out, nand_4_out, nand_7_out, nand_8_out,
       nand_9_out, nand_10_out, not_1_out, not_2_out, not_3_out, not_4_out, not_5_out, not_6_out, not_7_out,
       not_8_out, not_9_out, not_10_out, not_11_out, not_12_out, or_1_out, or_2_out, or_3_out, or_4_out,
       or_5_out, or_6_out, or_7_out, or_8_out;

  not not_1 (not_1_out, DN);
  not not_2 (not_2_out, UP);
  not not_3 (not_3_out, CLR);
  not not_4 (not_4_out, nLD);
  PowerSupply powersupply_1 (.VDD(VCC), .GND(GND));
  nand nand_1 (nand_1_out, D0, not_4_out, not_3_out);
  nand nand_2 (nand_2_out, D1, not_4_out, not_3_out);
  and and_1 (and_1_out, not_1_out, jk_ff_as_1_nq);
  and and_2 (and_2_out, Q0, not_2_out);
  nand nand_3 (nand_3_out, D2, not_4_out, not_3_out);
  and and_3 (and_3_out, not_1_out, jk_ff_as_1_nq, jk_ff_as_2_nq);
  and and_4 (and_4_out, Q0, Q1, not_2_out);
  nand nand_4 (nand_4_out, D3, not_4_out, not_3_out);
  and and_5 (and_5_out, not_1_out, jk_ff_as_1_nq, jk_ff_as_2_nq, jk_ff_as_3_nq);
  and and_6 (and_6_out, Q0, Q1, Q2, not_2_out);
  nand nand_5 (nBO, not_1_out, jk_ff_as_1_nq, jk_ff_as_2_nq, jk_ff_as_3_nq, jk_ff_as_4_nq);
  nand nand_6 (nCO, Q0, Q1, Q2, Q3, not_2_out);
  or or_1 (or_1_out, not_1_out, not_2_out);
  or or_2 (or_2_out, and_1_out, and_2_out);
  or or_3 (or_3_out, and_3_out, and_4_out);
  or or_4 (or_4_out, and_5_out, and_6_out);
  nand nand_7 (nand_7_out, nand_1_out, not_4_out);
  nand nand_8 (nand_8_out, nand_2_out, not_4_out);
  nand nand_9 (nand_9_out, nand_3_out, not_4_out);
  nand nand_10 (nand_10_out, nand_4_out, not_4_out);
  not not_5 (not_5_out, or_1_out);
  or or_5 (or_5_out, ~not_3_out, ~nand_7_out);  // Or
  not not_6 (not_6_out, or_2_out);
  or or_6 (or_6_out, ~not_3_out, ~nand_8_out);  // Or
  not not_7 (not_7_out, or_3_out);
  or or_7 (or_7_out, ~not_3_out, ~nand_9_out);  // Or
  not not_8 (not_8_out, or_4_out);
  or or_8 (or_8_out, ~not_3_out, ~nand_10_out);  // Or
  not not_9 (not_9_out, nand_1_out);
  JK_FF_AS jk_ff_as_1 (.Set(not_9_out), .J(1'b1), .C(not_5_out), .K(1'b1), .Clr(or_5_out), .Q(Q0), .nQ(jk_ff_as_1_nq));
  not not_10 (not_10_out, nand_2_out);
  JK_FF_AS jk_ff_as_2 (.Set(not_10_out), .J(1'b1), .C(not_6_out), .K(1'b1), .Clr(or_6_out), .Q(Q1), .nQ(jk_ff_as_2_nq));
  not not_11 (not_11_out, nand_3_out);
  JK_FF_AS jk_ff_as_3 (.Set(not_11_out), .J(1'b1), .C(not_7_out), .K(1'b1), .Clr(or_7_out), .Q(Q2), .nQ(jk_ff_as_3_nq));
  not not_12 (not_12_out, nand_4_out);
  JK_FF_AS jk_ff_as_4 (.Set(not_12_out), .J(1'b1), .C(not_8_out), .K(1'b1), .Clr(or_8_out), .Q(Q3), .nQ(jk_ff_as_4_nq));

  // Notes on the sheet:
  //   nBO: Borrow Output, pin 13
  //   nCO: Carry Output, pin 12
  //   DN: Down Count, pin 4
  //   UP: Up Count, pin 5
  //   D0: Data Input 0, pin 15
  //   Q0: Output Q0, pin 3
  //   Q1: Output Q1, pin 2
  //   D1: Data Input 1, pin 1
  //   Q2: Output Q2, pin 6
  //   D2: Data Input 2, pin 10
  //   Q3: Output Q3, pin 7
  //   D3: Data Input 3, pin 9
  //   CLR: Clear, pin 14
  //   nLD: Load, pin 11
  //   VCC: pin 16, default 1
  //   GND: pin 8
endmodule

/* Test case Count:
CLR ~LD D0 D1 D2 D3 UP DN Q0 Q1 Q2 Q3 ~CO ~BO
0 1 0 0 0 0 1 1 X X X X 1 1
0 1 1 0 1 1 1 1 X X X X 1 1
1 1 1 0 1 1 1 1 0 0 0 0 1 1
0 1 1 0 1 1 1 1 0 0 0 0 1 1
0 0 1 0 1 1 1 1 1 0 1 1 1 1
0 1 X X X X 1 1 1 0 1 1 1 1
0 1 X X X X 0 1 1 0 1 1 1 1
0 1 X X X X 1 1 0 1 1 1 1 1
0 1 X X X X 0 1 0 1 1 1 1 1
0 1 X X X X 1 1 1 1 1 1 1 1
0 1 X X X X 0 1 1 1 1 1 0 1
0 1 X X X X 1 1 0 0 0 0 1 1
0 1 X X X X 0 1 0 0 0 0 1 1
0 1 X X X X 1 1 1 0 0 0 1 1
0 1 X X X X 0 1 1 0 0 0 1 1
0 1 X X X X 1 1 0 1 0 0 1 1
0 1 X X X X 1 0 0 1 0 0 1 1
0 1 X X X X 1 1 1 0 0 0 1 1
0 1 X X X X 1 0 1 0 0 0 1 1
0 1 X X X X 1 1 0 0 0 0 1 1
0 1 X X X X 1 0 0 0 0 0 1 0
0 1 X X X X 1 1 1 1 1 1 1 1
0 1 X X X X 1 0 1 1 1 1 1 1
0 1 X X X X 1 1 0 1 1 1 1 1
0 1 X X X X 1 0 0 1 1 1 1 1
0 1 X X X X 1 1 1 0 1 1 1 1
*/
