// Digital circuit ROM_sequencer.dig as structural Verilog
module ROM_sequencer (
  input  in_1,
  input  in_2,
  input  in_3,
  input  in_4,
  input  in_5,
  input  in_6,
  input  clk,
  input  in_8,
  output nLOAD,
  output nRES,
  output GCLK,
  output GATE,
  output Bout
);

  wire A0, A1, A2, A3, A4, A5, A6, A7, A8, A9, A10, A11, A12, A13, A14, A15, button_1_out, D0, D1, D2, D3,
       D4, D5, D6, D7, D8, D9, D10, D11, D12, D13, D14, D15, nand_1_out, nand_2_out, nand_3_out, nand_7_out,
       nCLRPC, nSET, PC_Cin, PC_DATA, PCin, PCout, U5_pin9, UP, xor_1_out, xor_2_out, xor_3_out;
  wire [3:0] U8_q0;

  Monoflop monoflop_1 (.C(nLOAD), .R(1'b0), .nQ(nRES));  // open: Q
  Monoflop monoflop_2 (.C(button_1_out), .R(1'b0), .nQ(nLOAD));  // open: Q
  Button button_1 (.out(button_1_out));
  _27C1024 U17 (
    .nCE(1'b0), .nOE(1'b0), .VPP(1'b1), .VDD(1'b1), .GND(1'b0), .I_O0(D0), .I_O1(D1), .I_O2(D2), .I_O3(D3),
    .I_O4(D4), .I_O5(D5), .I_O6(D6), .I_O7(D7), .A0(A0), .A1(A1), .A2(A2), .A3(A3), .A4(A4), .A5(A5),
    .A6(A6), .A7(A7), .A8(A8), .A9(A9), .A10(A10), .A11(A11), .A12(A12), .A13(A13), .A14(A14), .A15(A15),
    .I_O8(D8), .I_O9(D9), .I_O10(D10), .I_O11(D11), .I_O12(D12), .I_O13(D13), .I_O14(D14), .I_O15(D15),
    .VSS(1'b0));
  _74165 U5 (
    .pin1(nLOAD), .pin2(GCLK), .pin3(D11), .pin4(D10), .pin5(D9), .pin6(D8), .pin8(1'b0), .pin9(U5_pin9),
    .pin10(1'b0), .pin11(D15), .pin12(D14), .pin13(D13), .pin14(D12), .pin15(1'b0), .pin16(1'b1));  // open: pin7
  _7474 U14 (
    .pin1(1'b1), .pin2(1'b1), .pin3(1'b1), .pin4(1'b1), .pin7(1'b0), .pin9(PC_Cin), .pin10(nLOAD),
    .pin11(GCLK), .pin12(PC_DATA), .pin13(1'b1), .pin14(1'b1));  // open: pin5, pin6, pin8
  _74165 U6 (
    .pin1(nLOAD), .pin2(GCLK), .pin3(D3), .pin4(D2), .pin5(D1), .pin6(D0), .pin8(1'b0), .pin9(Bout),
    .pin10(U5_pin9), .pin11(D7), .pin12(D6), .pin13(D5), .pin14(D4), .pin15(1'b0), .pin16(1'b1));  // open: pin7
  nand nand_1 (nand_1_out, PCout, PC_Cin);
  xor xor_1 (xor_1_out, PCout, PC_Cin);
  xor xor_2 (xor_2_out, in_8, 1'b1);
  xor xor_3 (xor_3_out, in_1, xor_2_out);
  xor xor_4 (PC_DATA, nand_1_out, 1'b1);
  nand nand_2 (nand_2_out, xor_1_out, xor_3_out);
  nand nand_3 (nand_3_out, xor_2_out, Bout);
  nand nand_4 (PCin, nand_2_out, nand_3_out);
  Seven_Seg_Hex seven_seg_hex_1 (.d(U8_q0), .dp(1'b0));
  Reset reset_1 (.out(nCLRPC));
  _74595 U19 (
    .pin1(A14), .pin2(A13), .pin3(A12), .pin4(A11), .pin5(A10), .pin6(A9), .pin7(A8), .pin8(1'b0),
    .pin10(nCLRPC), .pin11(GCLK), .pin12(GATE), .pin13(1'b0), .pin14(1'b0), .pin15(A15), .pin16(1'b1));  // open: pin9
  _74193 U8 (
    .nBO(nSET), .DN(GCLK), .UP(1'b1), .D0(in_2), .Q0(U8_q0[0]), .Q1(U8_q0[1]), .D1(in_3), .Q2(U8_q0[2]),
    .D2(in_4), .Q3(U8_q0[3]), .D3(in_5), .CLR(in_6), .nLD(nRES), .VCC(1'b1), .GND(1'b0));  // open: nCO
  _74595 U20 (
    .pin1(A6), .pin2(A5), .pin3(A4), .pin4(A3), .pin5(A2), .pin6(A1), .pin7(A0), .pin8(1'b0), .pin9(PCout),
    .pin10(nCLRPC), .pin11(GCLK), .pin12(GATE), .pin13(1'b0), .pin14(PCin), .pin15(A7), .pin16(1'b1));
  Seven_Seg_Hex seven_seg_hex_2 (.d({D15, D14, D13, D12}), .dp(1'b0));
  nand nand_5 (UP, nRES, GATE);
  nand nand_6 (GATE, UP, nSET);
  Seven_Seg_Hex seven_seg_hex_3 (.d({D11, D10, D9, D8}), .dp(1'b0));
  Seven_Seg_Hex seven_seg_hex_4 (.d({A15, A14, A13, A12}), .dp(1'b0));
  nand nand_7 (nand_7_out, clk, UP);
  Seven_Seg_Hex seven_seg_hex_5 (.d({A11, A10, A9, A8}), .dp(1'b0));
  Seven_Seg_Hex seven_seg_hex_6 (.d({D7, D6, D5, D4}), .dp(1'b0));
  Seven_Seg_Hex seven_seg_hex_7 (.d({A7, A6, A5, A4}), .dp(1'b0));
  nand nand_8 (GCLK, nand_7_out, nand_7_out);
  Seven_Seg_Hex seven_seg_hex_8 (.d({D3, D2, D1, D0}), .dp(1'b0));
  Seven_Seg_Hex seven_seg_hex_9 (.d({A3, A2, A1, A0}), .dp(1'b0));

  // Other names for the same wires on the sheet: DB0 = D0; DB1 = D1; DB2 = D2; DB3 = D3; DB4 = D4; DB5 = D5; DB6 = D6;
  //   DB7 = D7; IR0 = D8; IR1 = D9; IR2 = D10; IR3 = D11; IR4 = D12; IR5 = D13; IR6 = D14; IR7 = D15; nJMP = in_8;
  //   T0 = nSET; R_nC = in_1; RCLK = GATE

  // Notes on the sheet:
  //   in_1: default 1
  //   in_2: default 1
  //   in_3: default 1
  //   in_4: default 1
  //   in_5: default 1
  //   clk: Hz: 4
  //   in_8: default 1
  //   16-bit serial ROM sequencer
  //   Program Counter and MAR
  //   16-bit Shift Register B
  //   Carry FF
  //   PC Carry FF
  //   1
  //   U15A
  //   A
  //   2
  //   U14A
  //   U14C
  //   9
  //   10
  //   C
  //   PC Incrementer/Loader
  //   3
  //   4
  //   5
  //   8
  //   12
  //   13
  //   B
  //   U14B
  //   U14D
  //   D
  //   6
  //   11
  //   U15D
  //   U15B
  //   U15C
  //   # Clock
  //   Input (15-S) Pulses
  //   U13
  //   PROGRAM COUNTER
endmodule
