// Digital circuit SHREK_1.dig as structural Verilog
module SHREK_1 (
  input  clk,
  input  in_2,
  input  in_3,
  input  in_4,
  output LD,
  output RES,
  output GCLK,
  output T0,
  output nRST,
  output RUN,
  output RCO
);

  wire A0, A1, A2, A3, A4, A5, A6, A7, A8, A9, A10, A11, A12, A13, A14, A15, ADD, ALU_CARRY, ALU_SUM, AND,
       Aout, Bout, button_1_out, button_2_out, button_3_out, button_4_out, button_5_out, button_6_out,
       button_7_out, button_8_out, button_9_out, button_10_out, button_11_out, button_12_out, button_13_out,
       button_14_out, button_15_out, button_16_out, button_17_out, button_18_out, C, Cin, CLA, CLR, Cout, D0,
       D1, D2, D3, D4, D5, D6, D7, D8, D9, D10, D11, D12, D13, D14, D15, d_ff_1_nq, d_ff_2_nq, d_ff_3_nq,
       d_ff_4_nq, d_ff_5_nq, d_ff_6_nq, d_ff_7_nq, d_ff_8_nq, d_ff_9_nq, d_ff_10_nq, d_ff_11_nq, d_ff_12_nq,
       diodebackward_1_out, diodebackward_3_out, diodebackward_9_out, F, Fout, GATE, I0, I1, IC17_2_nq,
       IC17_3_nq, IC17_4_nq, IC17_nq, LD_t, LOAD, nA, nand_1_out, nand_6_out, nand_7_out, nand_8_out, nB,
       nCLRPC, nJMP, OR, PC_CARRY, PC_CARRYIN, PC_DATA_IN, PC_SUM, PCout, pullup_2_out, pullup_4_out,
       pullup_5_out, pullup_7_out, SETC, ST, SUB, U3_pin9, U5_pin9, U11_pin8, U11_pin11, U16_pin14, XOR,
       xor_1_out, xor_4_out, ZERO;
  wire [3:0] U8_pin11, U9_pin3, U9_pin10, U10_pin3;
  wire [3:1] U10_pin10;

  Monoflop monoflop_1 (.C(LD), .R(1'b0), .Q(SETC), .nQ(RES));
  Monoflop monoflop_2 (.C(button_1_out), .R(1'b0), .Q(LD_t), .nQ(LD));
  Button button_1 (.out(button_1_out));
  Seven_Seg_Hex seven_seg_hex_1 (.d(U9_pin3), .dp(1'b0));
  _74164 U9 (
    .pin1(1'b1), .pin2(Fout), .pin3(U9_pin3[3]), .pin4(U9_pin3[2]), .pin5(U9_pin3[1]), .pin6(U9_pin3[0]),
    .pin7(1'b0), .pin8(GCLK), .pin9(CLR), .pin10(U9_pin10[3]), .pin11(U9_pin10[2]), .pin12(U9_pin10[1]),
    .pin13(U9_pin10[0]), .pin14(1'b1));
  Seven_Seg_Hex seven_seg_hex_2 (.d(U9_pin10), .dp(1'b0));
  Monoflop monoflop_3 (.C(button_2_out), .R(1'b0), .nQ(nCLRPC));  // open: Q
  Button button_2 (.out(button_2_out));
  Seven_Seg_Hex seven_seg_hex_3 (.d(U10_pin3), .dp(1'b0));
  Seven_Seg_Hex seven_seg_hex_4 (.d({U10_pin10, Aout}), .dp(1'b0));
  _74138 U1 (
    .pin1(in_2), .pin2(in_3), .pin3(in_4), .pin4(1'b0), .pin5(1'b0), .pin6(1'b1), .pin7(nJMP), .pin8(1'b0),
    .pin9(ST), .pin10(SUB), .pin11(ADD), .pin12(XOR), .pin13(OR), .pin14(AND), .pin15(LOAD), .pin16(1'b1));
  _74164 U10 (
    .pin1(1'b1), .pin2(U9_pin10[0]), .pin3(U10_pin3[3]), .pin4(U10_pin3[2]), .pin5(U10_pin3[1]),
    .pin6(U10_pin3[0]), .pin7(1'b0), .pin8(GCLK), .pin9(CLR), .pin10(U10_pin10[3]), .pin11(U10_pin10[2]),
    .pin12(U10_pin10[1]), .pin13(Aout), .pin14(1'b1));
  DiodeBackward diodebackward_1 (.in(LOAD), .out(diodebackward_1_out));
  DiodeBackward diodebackward_2 (.in(nJMP), .out(diodebackward_1_out));
  PullUp pullup_1 (.out(diodebackward_1_out));
  DiodeBackward diodebackward_3 (.in(LOAD), .out(diodebackward_3_out));
  DiodeBackward diodebackward_4 (.in(ADD), .out(diodebackward_3_out));
  DiodeBackward diodebackward_5 (.in(SUB), .out(diodebackward_3_out));
  DiodeBackward diodebackward_6 (.in(nJMP), .out(diodebackward_3_out));
  PullUp pullup_2 (.out(pullup_2_out));
  PullUp pullup_3 (.out(diodebackward_3_out));
  DiodeBackward diodebackward_7 (.in(SUB), .out(pullup_2_out));
  PullUp pullup_4 (.out(pullup_4_out));
  DiodeBackward diodebackward_8 (.in(SUB), .out(pullup_4_out));
  PullUp pullup_5 (.out(pullup_5_out));
  DiodeBackward diodebackward_9 (.in(AND), .out(diodebackward_9_out));
  DiodeBackward diodebackward_10 (.in(OR), .out(diodebackward_9_out));
  _74165 U3 (
    .pin1(LD), .pin2(GCLK), .pin3(D11), .pin4(D10), .pin5(D9), .pin6(D8), .pin8(1'b0), .pin9(U3_pin9),
    .pin10(1'b0), .pin11(D15), .pin12(D14), .pin13(D13), .pin14(D12), .pin15(1'b0), .pin16(1'b1));  // open: pin7
  PullUp pullup_6 (.out(diodebackward_9_out));
  PullUp pullup_7 (.out(pullup_7_out));
  DiodeBackward diodebackward_11 (.in(LOAD), .out(pullup_7_out));
  DiodeBackward diodebackward_12 (.in(OR), .out(pullup_7_out));
  DiodeBackward diodebackward_13 (.in(XOR), .out(pullup_7_out));
  DiodeBackward diodebackward_14 (.in(ADD), .out(pullup_7_out));
  DiodeBackward diodebackward_15 (.in(SUB), .out(pullup_7_out));
  DiodeBackward diodebackward_16 (.in(ST), .out(pullup_7_out));
  DiodeBackward diodebackward_17 (.in(nJMP), .out(pullup_7_out));
  _74540 U2 (
    .pin1(1'b0), .pin2(pullup_7_out), .pin3(diodebackward_9_out), .pin4(pullup_5_out), .pin5(pullup_4_out),
    .pin6(pullup_2_out), .pin7(diodebackward_3_out), .pin8(diodebackward_1_out), .pin9(1'b0), .pin10(1'b0),
    .pin11(ZERO), .pin12(CLA), .pin13(F), .pin14(C), .pin15(nB), .pin16(nA), .pin17(I1), .pin18(I0),
    .pin19(1'b0), .pin20(1'b1));
  _74165 U4 (
    .pin1(LD), .pin2(GCLK), .pin3(D3), .pin4(D2), .pin5(D1), .pin6(D0), .pin8(1'b0), .pin9(Bout),
    .pin10(U3_pin9), .pin11(D7), .pin12(D6), .pin13(D5), .pin14(D4), .pin15(1'b0), .pin16(1'b1));  // open: pin7
  LED led_1 (.in(D15));
  D_FF IC17 (.D(IC17_nq), .C(button_3_out), .Q(D15), .nQ(IC17_nq));
  LED led_2 (.in(D14));
  D_FF d_ff_1 (.D(d_ff_1_nq), .C(button_4_out), .Q(D14), .nQ(d_ff_1_nq));
  Button button_3 (.out(button_3_out));
  LED led_3 (.in(D13));
  D_FF d_ff_2 (.D(d_ff_2_nq), .C(button_5_out), .Q(D13), .nQ(d_ff_2_nq));
  Button button_4 (.out(button_4_out));
  LED led_4 (.in(D12));
  D_FF d_ff_3 (.D(d_ff_3_nq), .C(button_6_out), .Q(D12), .nQ(d_ff_3_nq));
  Button button_5 (.out(button_5_out));
  LED led_5 (.in(D11));
  D_FF d_ff_4 (.D(d_ff_4_nq), .C(button_7_out), .Q(D11), .nQ(d_ff_4_nq));
  Button button_6 (.out(button_6_out));
  LED led_6 (.in(D10));
  D_FF d_ff_5 (.D(d_ff_5_nq), .C(button_8_out), .Q(D10), .nQ(d_ff_5_nq));
  Button button_7 (.out(button_7_out));
  _74595 U5 (
    .pin1(A14), .pin2(A13), .pin3(A12), .pin4(A11), .pin5(A10), .pin6(A9), .pin7(A8), .pin8(1'b0),
    .pin9(U5_pin9), .pin10(nCLRPC), .pin11(GCLK), .pin12(nRST), .pin13(1'b0), .pin14(PC_DATA_IN),
    .pin15(A15), .pin16(1'b1));
  LED led_7 (.in(D9));
  D_FF d_ff_6 (.D(d_ff_6_nq), .C(button_9_out), .Q(D9), .nQ(d_ff_6_nq));
  Button button_8 (.out(button_8_out));
  LED led_8 (.in(D8));
  D_FF IC17_2 (.D(IC17_2_nq), .C(button_10_out), .Q(D8), .nQ(IC17_2_nq));
  Button button_9 (.out(button_9_out));
  Button button_10 (.out(button_10_out));
  Seven_Seg_Hex seven_seg_hex_5 (.d({D15, D14, D13, D12}), .dp(1'b0));
  _74595 U6 (
    .pin1(A6), .pin2(A5), .pin3(A4), .pin4(A3), .pin5(A2), .pin6(A1), .pin7(A0), .pin8(1'b0), .pin9(PCout),
    .pin10(nCLRPC), .pin11(GCLK), .pin12(nRST), .pin13(1'b0), .pin14(U5_pin9), .pin15(A7), .pin16(1'b1));
  Seven_Seg_Hex seven_seg_hex_6 (.d({D11, D10, D9, D8}), .dp(1'b0));
  LED led_9 (.in(D7));
  D_FF IC17_3 (.D(IC17_3_nq), .C(button_11_out), .Q(D7), .nQ(IC17_3_nq));
  Button button_11 (.out(button_11_out));
  LED led_10 (.in(D6));
  D_FF d_ff_7 (.D(d_ff_7_nq), .C(button_12_out), .Q(D6), .nQ(d_ff_7_nq));
  Button button_12 (.out(button_12_out));
  LED led_11 (.in(D5));
  D_FF d_ff_8 (.D(d_ff_8_nq), .C(button_13_out), .Q(D5), .nQ(d_ff_8_nq));
  Button button_13 (.out(button_13_out));
  Seven_Seg_Hex seven_seg_hex_7 (.d({A15, A14, A13, A12}), .dp(1'b0));
  LED led_12 (.in(D4));
  D_FF d_ff_9 (.D(d_ff_9_nq), .C(button_14_out), .Q(D4), .nQ(d_ff_9_nq));
  Button button_14 (.out(button_14_out));
  Seven_Seg_Hex seven_seg_hex_8 (.d({A11, A10, A9, A8}), .dp(1'b0));
  LED led_13 (.in(D3));
  D_FF d_ff_10 (.D(d_ff_10_nq), .C(button_15_out), .Q(D3), .nQ(d_ff_10_nq));
  Button button_15 (.out(button_15_out));
  Seven_Seg_Hex seven_seg_hex_9 (.d({A7, A6, A5, A4}), .dp(1'b0));
  LED led_14 (.in(D2));
  D_FF d_ff_11 (.D(d_ff_11_nq), .C(button_16_out), .Q(D2), .nQ(d_ff_11_nq));
  Button button_16 (.out(button_16_out));
  Seven_Seg_Hex seven_seg_hex_10 (.d({A3, A2, A1, A0}), .dp(1'b0));
  LED led_15 (.in(D1));
  D_FF d_ff_12 (.D(d_ff_12_nq), .C(button_17_out), .Q(D1), .nQ(d_ff_12_nq));
  Button button_17 (.out(button_17_out));
  LED led_16 (.in(D0));
  D_FF IC17_4 (.D(IC17_4_nq), .C(button_18_out), .Q(D0), .nQ(IC17_4_nq));
  Button button_18 (.out(button_18_out));
  Seven_Seg_Hex seven_seg_hex_11 (.d({D7, D6, D5, D4}), .dp(1'b0));
  nand nand_1 (nand_1_out, clk, clk);
  nand nand_2 (GATE, RES, nRST);
  nand nand_3 (nRST, GATE, T0);
  Seven_Seg_Hex seven_seg_hex_12 (.d({D3, D2, D1, D0}), .dp(1'b0));
  nand nand_4 (GCLK, nand_1_out, GATE);
  _74283 U16 (
    .pin1(PC_CARRY), .pin2(1'b0), .pin3(1'b0), .pin4(PC_SUM), .pin5(1'b0), .pin6(PCout), .pin7(PC_CARRYIN),
    .pin8(1'b0), .pin9(ALU_CARRY), .pin10(ALU_SUM), .pin11(Cin), .pin12(Aout), .pin14(U16_pin14),
    .pin15(1'b1), .pin16(1'b1));  // open: pin13
  nand nand_5 (CLR, CLA, LD_t);
  xor xor_1 (xor_1_out, 1'b1, C);
  nand nand_6 (nand_6_out, C, SETC);
  _74161 U8 (
    .pin1(GATE), .pin2(clk), .pin3(1'b0), .pin4(1'b0), .pin5(1'b0), .pin6(1'b0), .pin7(1'b1), .pin8(1'b0),
    .pin9(1'b1), .pin10(1'b1), .pin11(U8_pin11[3]), .pin12(U8_pin11[2]), .pin13(U8_pin11[1]),
    .pin14(U8_pin11[0]), .pin15(RCO), .pin16(1'b1));
  nand nand_7 (nand_7_out, LD_t, xor_1_out);
  xor xor_2 (U16_pin14, Bout, nB);
  nand nand_8 (nand_8_out, ALU_CARRY, F);
  Seven_Seg_Hex seven_seg_hex_13 (.d(U8_pin11), .dp(1'b0));
  xor xor_3 (Cout, 1'b1, nand_8_out);
  _7474 U13 (
    .pin1(nand_7_out), .pin2(Cout), .pin3(GCLK), .pin4(nand_6_out), .pin5(Cin), .pin7(1'b0), .pin8(T0),
    .pin9(RUN), .pin10(1'b1), .pin11(clk), .pin12(RCO), .pin13(1'b1), .pin14(1'b1));  // open: pin6
  xor xor_4 (xor_4_out, 1'b1, nJMP);
  PullDown pulldown_1 (.out(nJMP));
  _74126 U11 (
    .pin1(nJMP), .pin2(PC_SUM), .pin3(PC_DATA_IN), .pin4(xor_4_out), .pin5(Bout), .pin6(PC_DATA_IN),
    .pin7(1'b0), .pin8(U11_pin8), .pin9(ALU_CARRY), .pin10(I1), .pin11(U11_pin11), .pin12(ALU_SUM),
    .pin13(I0), .pin14(1'b1));
  _7474 U15 (
    .pin1(1'b1), .pin2(1'b1), .pin3(1'b1), .pin4(1'b1), .pin7(1'b0), .pin9(PC_CARRYIN), .pin10(LD),
    .pin11(GCLK), .pin12(PC_CARRY), .pin13(1'b1), .pin14(1'b1));  // open: pin5, pin6, pin8
  DiodeForward diodeforward_1 (.in(U11_pin11), .out(Fout));
  DiodeForward diodeforward_2 (.in(U11_pin8), .out(Fout));
  PullDown pulldown_2 (.out(Fout));

  // Other names for the same wires on the sheet: IR4 = in_2; IR5 = in_3; IR6 = in_4; RST = nCLRPC; nLOAD = LD;
  //   nRES = RES; nSS = nRST; RCLK = nRST; PC_CARRYOUT = PC_CARRY

  // Notes on the sheet:
  //   clk: Hz: 2
  //   STEP/RUN
  //   ACCUMULATOR
  //   CLR PC
  //   Shift Register A
  //   Instruction Input
  //   Instruction Decode
  //   CLA
  //   C
  //   F
  //   ~B
  //   ~A
  //   I0
  //   I1
  //   LOAD
  //   AND
  //   OR
  //   XOR
  //   ADD
  //   SUB
  //   STORE
  //   JMP
  //   8-bit Shift Register B
  //   ENTER H
  //   PROGRAM MEMORY  ADDRESS REGISTER
  //   Data Input
  //   ENTER L
  //   PROGRAM COUNTER
  //   U7
  //   16-bit, Bit Serial CPU Testbed
  //   ALU
  //   Clock Sequencer
  //   6 Package Bit Serial ALU & PC Incrementer/Loader
  //   U12
  //   Suppress Carry
  //   # Clock
  //   U14
  //   Carry FF
  //   PC/ALU MUX
  //   PC Carry FF
endmodule
