// Digital circuit SPIder_June_19_2024.dig as structural Verilog
module SPIder_June_19_2024 (
  input  clk,
  input  in_2,
  input  in_3,
  input  in_4,
  input  S0,
  input  S1,
  input  S2,
  input  S3,
  input  in_13,
  input  in_15,
  input  in_16,
  input  nWR,
  input  in_18,
  input  nRD,
  input  in_20,
  output LD,
  output RES,
  output GCLK,
  output T0,
  output nSET1
);

  wire A0, A1, A2, A3, A4, A5, A6, A7, A8, A9, A10, A11, A12, A13, A14, A15, A_out, ADD, AND, Aout, Bout,
       BUS0, BUS1, BUS2, BUS3, BUS4, BUS5, BUS6, BUS7, BUS8, BUS9, BUS10, BUS11, BUS12, BUS13, BUS14, BUS15,
       button_1_out, button_2_out, button_3_out, button_4_out, button_5_out, button_6_out, button_7_out,
       button_8_out, button_9_out, button_10_out, button_11_out, button_12_out, button_13_out, button_14_out,
       button_15_out, button_16_out, button_17_out, button_18_out, C, Cin, CLA, CLR, Cout, D0, D1, D2, D3,
       D4, D5, D6, D7, D8, D9, D10, D11, D12, D13, D14, D15, d_ff_1_nq, d_ff_2_nq, d_ff_3_nq, d_ff_4_nq,
       d_ff_5_nq, d_ff_6_nq, d_ff_7_nq, d_ff_8_nq, d_ff_9_nq, d_ff_10_nq, d_ff_11_nq, d_ff_12_nq, DB0, DB1,
       DB2, DB3, DB4, DB5, DB6, DB7, diodebackward_1_out, diodebackward_2_out, diodebackward_8_out,
       diodebackward_9_out, F, Fout, I0, I1, IC16_2_nq, IC16_nq, IC17_2_nq, IC17_nq, IR0, IR1, IR2, IR3, IR4,
       IR5, IR6, IR7, LD_t, LOAD, nA, nand_1_out, nand_2_out, nand_3_out, nand_5_out, nand_6_out, nand_8_out,
       nand_9_out, nand_10_out, nand_11_out, nand_12_out, nand_13_out, nand_14_out, nand_19_out, nB, nCLRPC,
       nJMP, OR, PC_Cin, PC_DATA, PCin, PCout, pullup_2_out, pullup_4_out, pullup_7_out, RCLK, SETC, ST, SUB,
       U3_pin9, UP, XOR, xor_1_out, xor_2_out, xor_3_out, xor_5_out, xor_6_out, xor_7_out, xor_8_out;
  wire [3:0] U7_q0;

  Monoflop monoflop_1 (.C(LD), .R(1'b0), .Q(SETC), .nQ(RES));
  Monoflop monoflop_2 (.C(button_1_out), .R(1'b0), .Q(LD_t), .nQ(LD));
  Button button_1 (.out(button_1_out));
  _74165 U3 (
    .pin1(LD), .pin2(GCLK), .pin3(D11), .pin4(D10), .pin5(D9), .pin6(D8), .pin8(1'b0), .pin9(U3_pin9),
    .pin10(1'b0), .pin11(D15), .pin12(D14), .pin13(D13), .pin14(D12), .pin15(1'b0), .pin16(1'b1));  // open: pin7
  _74138 U1 (
    .pin1(in_2), .pin2(in_3), .pin3(in_4), .pin4(1'b0), .pin5(1'b0), .pin6(1'b1), .pin7(nJMP), .pin8(1'b0),
    .pin9(ST), .pin10(SUB), .pin11(ADD), .pin12(XOR), .pin13(OR), .pin14(AND), .pin15(LOAD), .pin16(1'b1));
  DiodeBackward diodebackward_1 (.in(LOAD), .out(diodebackward_1_out));
  Monoflop monoflop_3 (.C(T0), .R(1'b0), .nQ(nSET1));  // open: Q
  PullUp pullup_1 (.out(diodebackward_1_out));
  DiodeBackward diodebackward_2 (.in(LOAD), .out(diodebackward_2_out));
  DiodeBackward diodebackward_3 (.in(ADD), .out(diodebackward_2_out));
  DiodeBackward diodebackward_4 (.in(SUB), .out(diodebackward_2_out));
  DiodeBackward diodebackward_5 (.in(nJMP), .out(diodebackward_2_out));
  PullUp pullup_2 (.out(pullup_2_out));
  PullUp pullup_3 (.out(diodebackward_2_out));
  DiodeBackward diodebackward_6 (.in(SUB), .out(pullup_2_out));
  _74165 U4 (
    .pin1(LD), .pin2(GCLK), .pin3(D3), .pin4(D2), .pin5(D1), .pin6(D0), .pin8(1'b0), .pin9(Bout),
    .pin10(U3_pin9), .pin11(D7), .pin12(D6), .pin13(D5), .pin14(D4), .pin15(1'b0), .pin16(1'b1));  // open: pin7
  PullUp pullup_4 (.out(pullup_4_out));
  DiodeBackward diodebackward_7 (.in(SUB), .out(pullup_4_out));
  DiodeBackward diodebackward_8 (.in(nJMP), .out(diodebackward_8_out));
  nand nand_1 (nand_1_out, PCout, PC_Cin);
  xor xor_1 (xor_1_out, PCout, PC_Cin);
  xor xor_2 (xor_2_out, nJMP, 1'b1);
  PullUp pullup_5 (.out(diodebackward_8_out));
  DiodeBackward diodebackward_9 (.in(AND), .out(diodebackward_9_out));
  DiodeBackward diodebackward_10 (.in(OR), .out(diodebackward_9_out));
  xor xor_3 (xor_3_out, in_15, xor_2_out);
  PullUp pullup_6 (.out(diodebackward_9_out));
  PullUp pullup_7 (.out(pullup_7_out));
  DiodeBackward diodebackward_11 (.in(LOAD), .out(pullup_7_out));
  DiodeBackward diodebackward_12 (.in(OR), .out(pullup_7_out));
  DiodeBackward diodebackward_13 (.in(XOR), .out(pullup_7_out));
  DiodeBackward diodebackward_14 (.in(ADD), .out(pullup_7_out));
  DiodeBackward diodebackward_15 (.in(SUB), .out(pullup_7_out));
  DiodeBackward diodebackward_16 (.in(ST), .out(pullup_7_out));
  DiodeBackward diodebackward_17 (.in(nJMP), .out(pullup_7_out));
  _74540 U2 (
    .pin1(1'b0), .pin2(pullup_7_out), .pin3(diodebackward_9_out), .pin4(diodebackward_8_out),
    .pin5(pullup_4_out), .pin6(pullup_2_out), .pin7(diodebackward_2_out), .pin8(diodebackward_1_out),
    .pin9(1'b0), .pin10(1'b0), .pin12(CLA), .pin13(F), .pin14(C), .pin15(nB), .pin16(nA), .pin17(I1),
    .pin18(I0), .pin19(1'b0), .pin20(1'b1));  // open: pin11
  xor xor_4 (PC_DATA, nand_1_out, 1'b1);
  nand nand_2 (nand_2_out, xor_1_out, xor_3_out);
  nand nand_3 (nand_3_out, xor_2_out, Bout);
  nand nand_4 (PCin, nand_2_out, nand_3_out);
  LED led_1 (.in(D15));
  D_FF IC17 (.D(IC17_nq), .C(button_2_out), .Q(D15), .nQ(IC17_nq));
  LED led_2 (.in(D14));
  D_FF d_ff_1 (.D(d_ff_1_nq), .C(button_3_out), .Q(D14), .nQ(d_ff_1_nq));
  Button button_2 (.out(button_2_out));
  LED led_3 (.in(D13));
  D_FF d_ff_2 (.D(d_ff_2_nq), .C(button_4_out), .Q(D13), .nQ(d_ff_2_nq));
  Button button_3 (.out(button_3_out));
  _74595 U17 (
    .pin1(A14), .pin2(A13), .pin3(A12), .pin4(A11), .pin5(A10), .pin6(A9), .pin7(A8), .pin8(1'b0),
    .pin10(nCLRPC), .pin11(GCLK), .pin12(RCLK), .pin13(1'b0), .pin14(1'b0), .pin15(A15), .pin16(1'b1));  // open: pin9
  LED led_4 (.in(D12));
  D_FF d_ff_3 (.D(d_ff_3_nq), .C(button_5_out), .Q(D12), .nQ(d_ff_3_nq));
  Button button_4 (.out(button_4_out));
  LED led_5 (.in(D11));
  D_FF d_ff_4 (.D(d_ff_4_nq), .C(button_6_out), .Q(D11), .nQ(d_ff_4_nq));
  Button button_5 (.out(button_5_out));
  LED led_6 (.in(D10));
  D_FF d_ff_5 (.D(d_ff_5_nq), .C(button_7_out), .Q(D10), .nQ(d_ff_5_nq));
  Button button_6 (.out(button_6_out));
  LED led_7 (.in(D9));
  D_FF d_ff_6 (.D(d_ff_6_nq), .C(button_8_out), .Q(D9), .nQ(d_ff_6_nq));
  Button button_7 (.out(button_7_out));
  _74595 U18 (
    .pin1(A6), .pin2(A5), .pin3(A4), .pin4(A3), .pin5(A2), .pin6(A1), .pin7(A0), .pin8(1'b0), .pin9(PCout),
    .pin10(nCLRPC), .pin11(GCLK), .pin12(RCLK), .pin13(1'b0), .pin14(PCin), .pin15(A7), .pin16(1'b1));
  LED led_8 (.in(D8));
  D_FF IC17_2 (.D(IC17_2_nq), .C(button_9_out), .Q(D8), .nQ(IC17_2_nq));
  Button button_8 (.out(button_8_out));
  Seven_Seg_Hex seven_seg_hex_1 (.d({D15, D14, D13, D12}), .dp(1'b0));
  Button button_9 (.out(button_9_out));
  Seven_Seg_Hex seven_seg_hex_2 (.d({D11, D10, D9, D8}), .dp(1'b0));
  LED led_9 (.in(D7));
  D_FF IC16 (.D(IC16_nq), .C(button_10_out), .Q(D7), .nQ(IC16_nq));
  Button button_10 (.out(button_10_out));
  Seven_Seg_Hex seven_seg_hex_3 (.d({A15, A14, A13, A12}), .dp(1'b0));
  LED led_10 (.in(D6));
  D_FF d_ff_7 (.D(d_ff_7_nq), .C(button_11_out), .Q(D6), .nQ(d_ff_7_nq));
  Button button_11 (.out(button_11_out));
  Seven_Seg_Hex seven_seg_hex_4 (.d({A11, A10, A9, A8}), .dp(1'b0));
  LED led_11 (.in(D5));
  D_FF d_ff_8 (.D(d_ff_8_nq), .C(button_12_out), .Q(D5), .nQ(d_ff_8_nq));
  Button button_12 (.out(button_12_out));
  Seven_Seg_Hex seven_seg_hex_5 (.d({A7, A6, A5, A4}), .dp(1'b0));
  LED led_12 (.in(D4));
  D_FF d_ff_9 (.D(d_ff_9_nq), .C(button_13_out), .Q(D4), .nQ(d_ff_9_nq));
  Button button_13 (.out(button_13_out));
  Seven_Seg_Hex seven_seg_hex_6 (.d({A3, A2, A1, A0}), .dp(1'b0));
  Monoflop monoflop_4 (.C(button_14_out), .R(1'b0), .nQ(nCLRPC));  // open: Q
  Button button_14 (.out(button_14_out));
  LED led_13 (.in(D3));
  D_FF d_ff_10 (.D(d_ff_10_nq), .C(button_15_out), .Q(D3), .nQ(d_ff_10_nq));
  Button button_15 (.out(button_15_out));
  Seven_Seg_Hex seven_seg_hex_7 (.d({DB7, DB6, DB5, DB4}), .dp(1'b0));
  LED led_14 (.in(D2));
  D_FF d_ff_11 (.D(d_ff_11_nq), .C(button_16_out), .Q(D2), .nQ(d_ff_11_nq));
  Button button_16 (.out(button_16_out));
  Seven_Seg_Hex seven_seg_hex_8 (.d({DB3, DB2, DB1, DB0}), .dp(1'b0));
  LED led_15 (.in(D1));
  D_FF d_ff_12 (.D(d_ff_12_nq), .C(button_17_out), .Q(D1), .nQ(d_ff_12_nq));
  Button button_17 (.out(button_17_out));
  Seven_Seg_Hex seven_seg_hex_9 (.d({BUS15, BUS14, BUS13, BUS12}), .dp(1'b0));
  LED led_16 (.in(D0));
  D_FF IC16_2 (.D(IC16_2_nq), .C(button_18_out), .Q(D0), .nQ(IC16_2_nq));
  Button button_18 (.out(button_18_out));
  Seven_Seg_Hex seven_seg_hex_10 (.d({BUS11, BUS10, BUS9, BUS8}), .dp(1'b0));
  Seven_Seg_Hex seven_seg_hex_11 (.d({D7, D6, D5, D4}), .dp(1'b0));
  Seven_Seg_Hex seven_seg_hex_12 (.d({BUS7, BUS6, BUS5, BUS4}), .dp(1'b0));
  Seven_Seg_Hex seven_seg_hex_13 (.d({D3, D2, D1, D0}), .dp(1'b0));
  Seven_Seg_Hex seven_seg_hex_14 (.d({BUS3, BUS2, BUS1, BUS0}), .dp(1'b0));
  xor xor_5 (xor_5_out, Aout, nA);
  xor xor_6 (xor_6_out, nB, Bout);
  nand nand_5 (nand_5_out, SETC, C);
  nand nand_6 (nand_6_out, C, C);
  nand nand_7 (CLR, CLA, LD_t);
  Seven_Seg_Hex seven_seg_hex_15 (.d(U7_q0), .dp(1'b0));
  xor xor_7 (xor_7_out, xor_5_out, xor_6_out);
  nand nand_8 (nand_8_out, nand_6_out, LD_t);
  _74299 _74299_1 (
    .pin1(in_16), .pin2(nWR), .pin3(nWR), .pin4(BUS14), .pin5(BUS12), .pin6(BUS10), .pin7(BUS8),
    .pin8(A_out), .pin9(CLR), .pin10(1'b0), .pin11(1'b0), .pin12(GCLK), .pin13(BUS9), .pin14(BUS11),
    .pin15(BUS13), .pin16(BUS15), .pin18(Fout), .pin19(in_18), .pin20(1'b1));  // open: pin17
  xor xor_8 (xor_8_out, xor_7_out, Cin);
  nand nand_9 (nand_9_out, xor_7_out, Cin);
  nand nand_10 (nand_10_out, xor_5_out, xor_6_out);
  _74193 U7 (
    .nBO(T0), .DN(GCLK), .UP(1'b1), .D0(S0), .Q0(U7_q0[0]), .Q1(U7_q0[1]), .D1(S1), .Q2(U7_q0[2]), .D2(S2),
    .Q3(U7_q0[3]), .D3(S3), .CLR(in_13), .nLD(RES), .VCC(1'b1), .GND(1'b0));  // open: nCO
  nand nand_11 (nand_11_out, nand_9_out, nand_10_out);
  nand nand_12 (nand_12_out, xor_8_out, I0);
  nand nand_13 (nand_13_out, I1, nand_11_out);
  nand nand_14 (nand_14_out, nand_11_out, F);
  nand nand_15 (Fout, nand_12_out, nand_13_out);
  nand nand_16 (Cout, nand_14_out, nand_14_out);
  _74299 _74299_2 (
    .pin1(in_16), .pin2(nWR), .pin3(nWR), .pin4(BUS6), .pin5(BUS4), .pin6(BUS2), .pin7(BUS0), .pin8(Aout),
    .pin9(CLR), .pin10(1'b0), .pin11(1'b0), .pin12(GCLK), .pin13(BUS1), .pin14(BUS3), .pin15(BUS5),
    .pin16(BUS7), .pin18(A_out), .pin19(in_18), .pin20(1'b1));  // open: pin17
  nand nand_17 (UP, RES, RCLK);
  nand nand_18 (RCLK, UP, T0);
  _7474 U13 (
    .pin1(nand_8_out), .pin2(Cout), .pin3(GCLK), .pin4(nand_5_out), .pin5(Cin), .pin7(1'b0), .pin9(PC_Cin),
    .pin10(LD), .pin11(GCLK), .pin12(PC_DATA), .pin13(1'b1), .pin14(1'b1));  // open: pin6, pin8
  nand nand_19 (nand_19_out, clk, UP);
  nand nand_20 (GCLK, nand_19_out, nand_19_out);
  _27C1024 U16 (
    .nCE(1'b0), .nOE(1'b0), .VPP(1'b1), .VDD(1'b1), .GND(1'b0), .I_O0(DB0), .I_O1(DB1), .I_O2(DB2),
    .I_O3(DB3), .I_O4(DB4), .I_O5(DB5), .I_O6(DB6), .I_O7(DB7), .A0(A0), .A1(A1), .A2(A2), .A3(A3), .A4(A4),
    .A5(A5), .A6(A6), .A7(A7), .A8(A8), .A9(A9), .A10(A10), .A11(A11), .A12(A12), .A13(A13), .A14(A14),
    .A15(A15), .I_O8(IR0), .I_O9(IR1), .I_O10(IR2), .I_O11(IR3), .I_O12(IR4), .I_O13(IR5), .I_O14(IR6),
    .I_O15(IR7), .VSS(1'b0));
  // _28c256 U19: pin names not known; wires that end beside it: A14, A12, DB7, DB6, DB5, DB4, DB3, DB2, DB1, DB0, BUS8, 1'b1, nWR, A13, A8, A9, A11, nRD, A10, 1'b0, BUS15
  // _28c256 U20: pin names not known; wires that end beside it: BUS9, BUS10, 1'b0, A14, A12, DB7, DB6, DB5, DB4, DB3, DB2, DB1, DB0, BUS0, BUS1, BUS2, 1'b0, BUS12, BUS11, 1'b1, nWR, A13, A8, A9, A11, nRD, A10, 1'b0, BUS7
  PullUp pullup_8 (.out(nWR));
  _74157 U12 (
    .pin1(in_20), .pin2(A0), .pin3(IR0), .pin4(DB0), .pin5(A1), .pin6(IR1), .pin7(DB1), .pin8(1'b0),
    .pin9(DB2), .pin10(IR2), .pin11(A2), .pin12(DB3), .pin13(IR3), .pin14(A3), .pin15(1'b0), .pin16(1'b1));

  // Other names for the same wires on the sheet: M0 = in_16; M1 = in_18; nADD_REG = in_20; nLOAD = LD; nRES = RES;
  //   nSET = T0; nWE = nWR; R_nC = in_15; RA0 = DB0; RA1 = DB1; RA2 = DB2; RA3 = DB3; RA4 = DB4; RA5 = DB5; RA6 = DB6;
  //   RA7 = DB7

  // Notes on the sheet:
  //   clk: Hz: 8
  //   S0: default 1
  //   S1: default 1
  //   S2: default 1
  //   S3: default 1
  //   in_15: default 1
  //   nRD: default 1
  //   Spider
  //   Program Counter and MAR
  //   Instruction Input
  //   STEP/RUN
  //   16-bit Shift Register B
  //   Instruction Decode
  //   CLA
  //   C
  //   F
  //   1
  //   2
  //   9
  //   10
  //   PC Incrementer/Loader
  //   ~B
  //   U15A
  //   A
  //   U14A
  //   U14C
  //   ~A
  //   3
  //   4
  //   5
  //   U14B
  //   8
  //   I0
  //   I1
  //   12
  //   13
  //   6
  //   B
  //   LOAD
  //   AND
  //   OR
  //   XOR
  //   ADD
  //   SUB
  //   STORE
  //   JMP
  //   U14D
  //   D
  //   U15D
  //   U15B
  //   11
  //   U15C
  //   PROGRAM MEMORY  ADDRESS REGISTER
  //   ENTER H
  //   Spider 16-bit  Bit serial CPU Testbed
  //   Data Input
  //   PROGRAM COUNTER
  //   CLR PC
  //   ENTER L
  //   ROM Payload Byte
  //   ACCUMULATOR
  //   BUS
  //   ******Shift Operations******
  //   S Field  	Operation
  //   0101	Left Shift 2
  //   0110	Left Shift 1	
  //   0111	No Shift	8-bit transfer
  //   1000	Right Shift 1
  //   1001	Right Shift 2
  //   1010	Right Shift 3		
  //   1011	Nybble Swap (bit shift)
  //   1100
  //   1110	No Shift 16-bit transfer
  //   MODE M1:M0
  //   00  HOLD
  //   01  SHIFT LEFT
  //   10  SHIFT RIGHT
  //   11  PARALLEL LOAD
  //   Variable Pulse Train Clock Sequencer
  //   ALU
  //   U9
  //   CLR ACC
  //   U12
  //   # Clock
  //   Input (15-S) Pulses
  //   U10
  //   Carry is only set before Bit 0 of an operation
  //   Any residual carry is cleared before an operation
  //   16-bit Shift Register A
  //   Suppress Carry
  //   U11
  //   U8
  //   Carry FF
  //   PC Carry FF
endmodule
